// Logisim project REGISTER.circ as structural Verilog
module main (
  input  Load,
  input  [3:0] DataIn,
  input  [21:0] DataIn_2,
  input  [4:0] DataIn_3,
  input  Count,
  input  reset,
  output [21:0] Dataout,
  output [3:0] Dataout_2,
  output [4:0] Dataout_3,
  output [21:0] Dataout_4,
  output [4:0] Dataout_5
);

  wire clock_1_out;

  Clock clock_1 (.out(clock_1_out));
  MBR mbr_1 (.Count(Count), .Load(Load), .DataIn(DataIn_2), .clock(clock_1_out), .reset(reset), .Dataout(Dataout));
  IR ir_1 (.Load(Load), .DataIn(DataIn), .clock(clock_1_out), .reset(reset), .Dataout(Dataout_2));
  MAR mar_1 (.Load(Load), .DataIn(DataIn_3), .clock(clock_1_out), .reset(reset), .Dataout(Dataout_3));
  AC ac_1 (.Load(Load), .DataIn(DataIn_2), .clock(clock_1_out), .reset(reset), .Dataout(Dataout_4));
  PC pc_1 (.Count(Count), .Load(Load), .DataIn(DataIn_3), .clock(clock_1_out), .reset(reset), .Dataout(Dataout_5));

  // Notes on the sheet:
  //   2207042
endmodule

module MBR (
  input  Count,
  input  Load,
  input  [21:0] DataIn,
  input  clock,
  input  reset,
  output [21:0] Dataout
);

  wire mbr_counter_5_bit_1_cout, mbr_counter_5_bit_2_cout, mbr_counter_5_bit_3_cout, mbr_counter_5_bit_4_cout;

  MBR_counter_5_bit mbr_counter_5_bit_1 (
    .Count(Count), .Load(Load), .DataIn(DataIn[4:0]), .clock(clock), .reset(reset), .Dataout(Dataout[4:0]),
    .Cout(mbr_counter_5_bit_1_cout));
  MBR_counter_5_bit mbr_counter_5_bit_2 (
    .Count(mbr_counter_5_bit_1_cout), .Load(Load), .DataIn(DataIn[9:5]), .clock(clock), .reset(reset),
    .Dataout(Dataout[9:5]), .Cout(mbr_counter_5_bit_2_cout));
  MBR_counter_5_bit mbr_counter_5_bit_3 (
    .Count(mbr_counter_5_bit_2_cout), .Load(Load), .DataIn(DataIn[14:10]), .clock(clock), .reset(reset),
    .Dataout(Dataout[14:10]), .Cout(mbr_counter_5_bit_3_cout));
  MBR_counter_5_bit mbr_counter_5_bit_4 (
    .Count(mbr_counter_5_bit_3_cout), .Load(Load), .DataIn(DataIn[19:15]), .clock(clock), .reset(reset),
    .Dataout(Dataout[19:15]), .Cout(mbr_counter_5_bit_4_cout));
  MBR_counter_2_bit mbr_counter_2_bit_1 (
    .Count(mbr_counter_5_bit_4_cout), .Load(Load), .DATAin1(DataIn[20]), .DATAin2(DataIn[21]), .Clock(clock),
    .Reset(reset), .DATAout1(Dataout[20]), .DATAout2(Dataout[21]));  // open: Cout

  // Notes on the sheet:
  //   2207042
endmodule

module IR (
  input  Load,
  input  [3:0] DataIn,
  input  clock,
  input  reset,
  output [3:0] Dataout
);

  wire and_1_out, and_2_out, and_3_out, and_4_out, and_5_out, and_6_out, and_7_out, and_8_out, not_1_out,
       not_2_out, or_1_out, or_2_out, or_3_out, or_4_out;

  not not_1 (not_1_out, Load);
  not not_2 (not_2_out, not_1_out);
  and and_1 (and_1_out, Dataout[0], not_1_out);
  and and_2 (and_2_out, DataIn[0], not_2_out);
  and and_3 (and_3_out, Dataout[1], not_1_out);
  and and_4 (and_4_out, DataIn[1], not_2_out);
  and and_5 (and_5_out, Dataout[2], not_1_out);
  and and_6 (and_6_out, DataIn[2], not_2_out);
  and and_7 (and_7_out, Dataout[3], not_1_out);
  and and_8 (and_8_out, DataIn[3], not_2_out);
  or or_1 (or_1_out, and_1_out, and_2_out);
  or or_2 (or_2_out, and_3_out, and_4_out);
  or or_3 (or_3_out, and_5_out, and_6_out);
  or or_4 (or_4_out, and_7_out, and_8_out);
  D_Flip_Flop d_ff_1 (.clk(clock), .D(or_1_out), .Q(Dataout[0]), .reset(reset));  // open: Qn, preset, en
  D_Flip_Flop d_ff_2 (.clk(clock), .D(or_2_out), .Q(Dataout[1]), .reset(reset));  // open: Qn, preset, en
  D_Flip_Flop d_ff_3 (.clk(clock), .D(or_3_out), .Q(Dataout[2]), .reset(reset));  // open: Qn, preset, en
  D_Flip_Flop d_ff_4 (.clk(clock), .D(or_4_out), .Q(Dataout[3]), .reset(reset));  // open: Qn, preset, en

  // Notes on the sheet:
  //   2207042
endmodule

module MAR (
  input  Load,
  input  [4:0] DataIn,
  input  clock,
  input  reset,
  output [4:0] Dataout
);

  wire and_1_out, and_2_out, and_3_out, and_4_out, and_5_out, and_6_out, and_7_out, and_8_out, and_9_out,
       and_10_out, not_1_out, not_2_out, or_1_out, or_2_out, or_3_out, or_4_out, or_5_out;

  not not_1 (not_1_out, Load);
  not not_2 (not_2_out, not_1_out);
  and and_1 (and_1_out, Dataout[0], not_1_out);
  and and_2 (and_2_out, DataIn[0], not_2_out);
  and and_3 (and_3_out, Dataout[1], not_1_out);
  and and_4 (and_4_out, DataIn[1], not_2_out);
  and and_5 (and_5_out, Dataout[2], not_1_out);
  and and_6 (and_6_out, DataIn[2], not_2_out);
  and and_7 (and_7_out, Dataout[3], not_1_out);
  and and_8 (and_8_out, DataIn[3], not_2_out);
  and and_9 (and_9_out, Dataout[4], not_1_out);
  and and_10 (and_10_out, DataIn[4], not_2_out);
  or or_1 (or_1_out, and_1_out, and_2_out);
  or or_2 (or_2_out, and_3_out, and_4_out);
  or or_3 (or_3_out, and_5_out, and_6_out);
  or or_4 (or_4_out, and_7_out, and_8_out);
  or or_5 (or_5_out, and_9_out, and_10_out);
  D_Flip_Flop d_ff_1 (.clk(clock), .D(or_1_out), .Q(Dataout[0]), .reset(reset));  // open: Qn, preset, en
  D_Flip_Flop d_ff_2 (.clk(clock), .D(or_2_out), .Q(Dataout[1]), .reset(reset));  // open: Qn, preset, en
  D_Flip_Flop d_ff_3 (.clk(clock), .D(or_3_out), .Q(Dataout[2]), .reset(reset));  // open: Qn, preset, en
  D_Flip_Flop d_ff_4 (.clk(clock), .D(or_4_out), .Q(Dataout[3]), .reset(reset));  // open: Qn, preset, en
  D_Flip_Flop d_ff_5 (.clk(clock), .D(or_5_out), .Q(Dataout[4]), .reset(reset));  // open: Qn, preset, en

  // Notes on the sheet:
  //   2207042
endmodule

module AC (
  input  Load,
  input  [21:0] DataIn,
  input  clock,
  input  reset,
  output [21:0] Dataout
);

  wire and_1_out, and_2_out, and_3_out, and_4_out, and_5_out, and_6_out, and_7_out, and_8_out, and_9_out,
       and_10_out, and_11_out, and_12_out, and_13_out, and_14_out, and_15_out, and_16_out, and_17_out,
       and_18_out, and_19_out, and_20_out, and_21_out, and_22_out, and_23_out, and_24_out, and_25_out,
       and_26_out, and_27_out, and_28_out, and_29_out, and_30_out, and_31_out, and_32_out, and_33_out,
       and_34_out, and_35_out, and_36_out, and_37_out, and_38_out, and_39_out, and_40_out, and_41_out,
       and_42_out, and_43_out, and_44_out, not_1_out, not_2_out, or_1_out, or_2_out, or_3_out, or_4_out,
       or_5_out, or_6_out, or_7_out, or_8_out, or_9_out, or_10_out, or_11_out, or_12_out, or_13_out,
       or_14_out, or_15_out, or_16_out, or_17_out, or_18_out, or_19_out, or_20_out, or_21_out, or_22_out;

  Clock clock_1 ();  // open: out
  not not_1 (not_1_out, Load);
  not not_2 (not_2_out, not_1_out);
  and and_1 (and_1_out, Dataout[0], not_1_out);
  and and_2 (and_2_out, DataIn[0], not_2_out);
  and and_3 (and_3_out, Dataout[1], not_1_out);
  and and_4 (and_4_out, DataIn[1], not_2_out);
  and and_5 (and_5_out, Dataout[2], not_1_out);
  and and_6 (and_6_out, DataIn[2], not_2_out);
  and and_7 (and_7_out, Dataout[3], not_1_out);
  and and_8 (and_8_out, DataIn[3], not_2_out);
  and and_9 (and_9_out, Dataout[4], not_1_out);
  and and_10 (and_10_out, DataIn[4], not_2_out);
  and and_11 (and_11_out, Dataout[5], not_1_out);
  and and_12 (and_12_out, DataIn[5], not_2_out);
  and and_13 (and_13_out, Dataout[6], not_1_out);
  and and_14 (and_14_out, DataIn[6], not_2_out);
  and and_15 (and_15_out, Dataout[7], not_1_out);
  and and_16 (and_16_out, DataIn[7], not_2_out);
  and and_17 (and_17_out, Dataout[8], not_1_out);
  and and_18 (and_18_out, DataIn[8], not_2_out);
  and and_19 (and_19_out, Dataout[9], not_1_out);
  and and_20 (and_20_out, DataIn[9], not_2_out);
  and and_21 (and_21_out, Dataout[10], not_1_out);
  and and_22 (and_22_out, DataIn[10], not_2_out);
  and and_23 (and_23_out, Dataout[11], not_1_out);
  and and_24 (and_24_out, DataIn[11], not_2_out);
  and and_25 (and_25_out, Dataout[12], not_1_out);
  and and_26 (and_26_out, DataIn[12], not_2_out);
  and and_27 (and_27_out, Dataout[13], not_1_out);
  and and_28 (and_28_out, DataIn[13], not_2_out);
  and and_29 (and_29_out, Dataout[14], not_1_out);
  and and_30 (and_30_out, DataIn[14], not_2_out);
  and and_31 (and_31_out, Dataout[15], not_1_out);
  and and_32 (and_32_out, DataIn[15], not_2_out);
  and and_33 (and_33_out, Dataout[16], not_1_out);
  and and_34 (and_34_out, DataIn[16], not_2_out);
  and and_35 (and_35_out, Dataout[17], not_1_out);
  and and_36 (and_36_out, DataIn[17], not_2_out);
  and and_37 (and_37_out, Dataout[18], not_1_out);
  and and_38 (and_38_out, DataIn[18], not_2_out);
  and and_39 (and_39_out, Dataout[19], not_1_out);
  and and_40 (and_40_out, DataIn[19], not_2_out);
  and and_41 (and_41_out, Dataout[20], not_1_out);
  and and_42 (and_42_out, DataIn[20], not_2_out);
  and and_43 (and_43_out, Dataout[21], not_1_out);
  and and_44 (and_44_out, DataIn[21], not_2_out);
  or or_1 (or_1_out, and_1_out, and_2_out);
  or or_2 (or_2_out, and_3_out, and_4_out);
  or or_3 (or_3_out, and_5_out, and_6_out);
  or or_4 (or_4_out, and_7_out, and_8_out);
  or or_5 (or_5_out, and_9_out, and_10_out);
  or or_6 (or_6_out, and_11_out, and_12_out);
  or or_7 (or_7_out, and_13_out, and_14_out);
  or or_8 (or_8_out, and_15_out, and_16_out);
  or or_9 (or_9_out, and_17_out, and_18_out);
  or or_10 (or_10_out, and_19_out, and_20_out);
  or or_11 (or_11_out, and_21_out, and_22_out);
  or or_12 (or_12_out, and_23_out, and_24_out);
  or or_13 (or_13_out, and_25_out, and_26_out);
  or or_14 (or_14_out, and_27_out, and_28_out);
  or or_15 (or_15_out, and_29_out, and_30_out);
  or or_16 (or_16_out, and_31_out, and_32_out);
  or or_17 (or_17_out, and_33_out, and_34_out);
  or or_18 (or_18_out, and_35_out, and_36_out);
  or or_19 (or_19_out, and_37_out, and_38_out);
  or or_20 (or_20_out, and_39_out, and_40_out);
  or or_21 (or_21_out, and_41_out, and_42_out);
  or or_22 (or_22_out, and_43_out, and_44_out);
  D_Flip_Flop d_ff_1 (.clk(clock), .D(or_1_out), .Q(Dataout[0]), .reset(reset));  // open: Qn, preset, en
  D_Flip_Flop d_ff_2 (.clk(clock), .D(or_2_out), .Q(Dataout[1]), .reset(reset));  // open: Qn, preset, en
  D_Flip_Flop d_ff_3 (.clk(clock), .D(or_3_out), .Q(Dataout[2]), .reset(reset));  // open: Qn, preset, en
  D_Flip_Flop d_ff_4 (.clk(clock), .D(or_4_out), .Q(Dataout[3]), .reset(reset));  // open: Qn, preset, en
  D_Flip_Flop d_ff_5 (.clk(clock), .D(or_5_out), .Q(Dataout[4]), .reset(reset));  // open: Qn, preset, en
  D_Flip_Flop d_ff_6 (.clk(clock), .D(or_6_out), .Q(Dataout[5]), .reset(reset));  // open: Qn, preset, en
  D_Flip_Flop d_ff_7 (.clk(clock), .D(or_7_out), .Q(Dataout[6]), .reset(reset));  // open: Qn, preset, en
  D_Flip_Flop d_ff_8 (.clk(clock), .D(or_8_out), .Q(Dataout[7]), .reset(reset));  // open: Qn, preset, en
  D_Flip_Flop d_ff_9 (.clk(clock), .D(or_9_out), .Q(Dataout[8]), .reset(reset));  // open: Qn, preset, en
  D_Flip_Flop d_ff_10 (.clk(clock), .D(or_10_out), .Q(Dataout[9]), .reset(reset));  // open: Qn, preset, en
  D_Flip_Flop d_ff_11 (.clk(clock), .D(or_11_out), .Q(Dataout[10]), .reset(reset));  // open: Qn, preset, en
  D_Flip_Flop d_ff_12 (.clk(clock), .D(or_12_out), .Q(Dataout[11]), .reset(reset));  // open: Qn, preset, en
  D_Flip_Flop d_ff_13 (.clk(clock), .D(or_13_out), .Q(Dataout[12]), .reset(reset));  // open: Qn, preset, en
  D_Flip_Flop d_ff_14 (.clk(clock), .D(or_14_out), .Q(Dataout[13]), .reset(reset));  // open: Qn, preset, en
  D_Flip_Flop d_ff_15 (.clk(clock), .D(or_15_out), .Q(Dataout[14]), .reset(reset));  // open: Qn, preset, en
  D_Flip_Flop d_ff_16 (.clk(clock), .D(or_16_out), .Q(Dataout[15]), .reset(reset));  // open: Qn, preset, en
  D_Flip_Flop d_ff_17 (.clk(clock), .D(or_17_out), .Q(Dataout[16]), .reset(reset));  // open: Qn, preset, en
  D_Flip_Flop d_ff_18 (.clk(clock), .D(or_18_out), .Q(Dataout[17]), .reset(reset));  // open: Qn, preset, en
  D_Flip_Flop d_ff_19 (.clk(clock), .D(or_19_out), .Q(Dataout[18]), .reset(reset));  // open: Qn, preset, en
  D_Flip_Flop d_ff_20 (.clk(clock), .D(or_20_out), .Q(Dataout[19]), .reset(reset));  // open: Qn, preset, en
  D_Flip_Flop d_ff_21 (.clk(clock), .D(or_21_out), .Q(Dataout[20]), .reset(reset));  // open: Qn, preset, en
  D_Flip_Flop d_ff_22 (.clk(clock), .D(or_22_out), .Q(Dataout[21]), .reset(reset));  // open: Qn, preset, en

  // Notes on the sheet:
  //   2207042
endmodule

module PC (
  input  Count,
  input  Load,
  input  [4:0] DataIn,
  input  clock,
  input  reset,
  output [4:0] Dataout
);

  wire and_1_out, and_2_out, and_3_out, and_4_out, and_5_out, and_6_out, and_7_out, and_8_out, and_9_out,
       and_10_out, and_11_out, and_12_out, and_13_out, and_14_out, and_15_out, not_1_out, not_2_out,
       not_3_out, not_4_out, not_5_out, not_6_out, not_7_out, or_1_out, or_2_out, or_3_out, or_4_out,
       or_5_out, or_6_out, or_7_out, or_8_out, or_9_out, or_10_out;

  Clock clock_1 ();  // open: out
  not not_1 (not_1_out, Load);
  not not_2 (not_2_out, DataIn[0]);
  not not_3 (not_3_out, DataIn[1]);
  not not_4 (not_4_out, DataIn[2]);
  not not_5 (not_5_out, DataIn[3]);
  not not_6 (not_6_out, DataIn[4]);
  and and_1 (and_1_out, Count, not_1_out);
  not not_7 (not_7_out, not_1_out);
  and and_2 (and_2_out, DataIn[0], not_7_out);
  and and_3 (and_3_out, not_2_out, not_7_out);
  and and_4 (and_4_out, DataIn[1], not_7_out);
  and and_5 (and_5_out, not_3_out, not_7_out);
  and and_6 (and_6_out, DataIn[2], not_7_out);
  and and_7 (and_7_out, not_4_out, not_7_out);
  and and_8 (and_8_out, DataIn[3], not_7_out);
  and and_9 (and_9_out, not_5_out, not_7_out);
  and and_10 (and_10_out, DataIn[4], not_7_out);
  and and_11 (and_11_out, not_6_out, not_7_out);
  and and_12 (and_12_out, Dataout[0], and_1_out);
  and and_13 (and_13_out, Dataout[1], Dataout[0], and_1_out);
  and and_14 (and_14_out, Dataout[2], Dataout[1], Dataout[0], and_1_out);
  and and_15 (and_15_out, Dataout[3], Dataout[2], Dataout[1], Dataout[0], and_1_out);
  or or_1 (or_1_out, and_2_out, and_1_out);
  or or_2 (or_2_out, and_1_out, and_3_out);
  or or_3 (or_3_out, and_4_out, and_12_out);
  or or_4 (or_4_out, and_12_out, and_5_out);
  or or_5 (or_5_out, and_6_out, and_13_out);
  or or_6 (or_6_out, and_13_out, and_7_out);
  or or_7 (or_7_out, and_8_out, and_14_out);
  or or_8 (or_8_out, and_14_out, and_9_out);
  or or_9 (or_9_out, and_10_out, and_15_out);
  or or_10 (or_10_out, and_15_out, and_11_out);
  J_K_Flip_Flop j_k_ff_1 (
    .J(or_1_out), .clk(clock), .K(or_2_out), .Q(Dataout[0]), .reset(reset));  // open: Qn, preset, en
  J_K_Flip_Flop j_k_ff_2 (
    .J(or_3_out), .clk(clock), .K(or_4_out), .Q(Dataout[1]), .reset(reset));  // open: Qn, preset, en
  J_K_Flip_Flop j_k_ff_3 (
    .J(or_5_out), .clk(clock), .K(or_6_out), .Q(Dataout[2]), .reset(reset));  // open: Qn, preset, en
  J_K_Flip_Flop j_k_ff_4 (
    .J(or_7_out), .clk(clock), .K(or_8_out), .Q(Dataout[3]), .reset(reset));  // open: Qn, preset, en
  J_K_Flip_Flop j_k_ff_5 (
    .J(or_9_out), .clk(clock), .K(or_10_out), .Q(Dataout[4]), .reset(reset));  // open: Qn, preset, en

  // Notes on the sheet:
  //   2207042
endmodule

module AC_shift (
  input  load,
  input  [21:0] Datain,
  input  Shift,
  input  \input ,
  input  cloak_prime,
  input  reset,
  output \output ,
  output [21:0] Dataout
);

  wire and_1_out, or_1_out;
  wire [21:0] multiplexer_1_out;

  and and_1 (and_1_out, Shift, cloak_prime);
  or or_1 (or_1_out, load, Shift);
  AC ac_1 (.Load(or_1_out), .DataIn(multiplexer_1_out), .clock(cloak_prime), .reset(reset), .Dataout(Dataout));
  Multiplexer #(.width(22)) multiplexer_1 (
    .in0(Datain), .in1({\input , Dataout[21:1]}), .out(multiplexer_1_out), .sel(Shift));  // open: en
  Clock clock_1 ();  // open: out
  D_Flip_Flop d_ff_1 (.clk(and_1_out), .D(Dataout[0]), .Q(\output ));  // open: Qn, preset, en, reset

  // Notes on the sheet:
  //   2207042
endmodule

// MBR c5
module MBR_counter_5_bit (
  input  Count,
  input  Load,
  input  [4:0] DataIn,
  input  clock,
  input  reset,
  output [4:0] Dataout,
  output Cout
);

  wire and_1_out, and_2_out, and_3_out, and_4_out, and_5_out, and_6_out, and_7_out, and_8_out, and_9_out,
       and_10_out, and_11_out, and_12_out, and_13_out, and_14_out, and_15_out, not_1_out, not_2_out,
       not_3_out, not_4_out, not_5_out, not_6_out, not_7_out, or_1_out, or_2_out, or_3_out, or_4_out,
       or_5_out, or_6_out, or_7_out, or_8_out, or_9_out, or_10_out;

  Clock clock_1 ();  // open: out
  not not_1 (not_1_out, Load);
  not not_2 (not_2_out, DataIn[0]);
  not not_3 (not_3_out, DataIn[1]);
  not not_4 (not_4_out, DataIn[2]);
  not not_5 (not_5_out, DataIn[3]);
  not not_6 (not_6_out, DataIn[4]);
  and and_1 (and_1_out, Count, not_1_out);
  not not_7 (not_7_out, not_1_out);
  and and_2 (and_2_out, DataIn[0], not_7_out);
  and and_3 (and_3_out, not_2_out, not_7_out);
  and and_4 (and_4_out, DataIn[1], not_7_out);
  and and_5 (and_5_out, not_3_out, not_7_out);
  and and_6 (and_6_out, DataIn[2], not_7_out);
  and and_7 (and_7_out, not_4_out, not_7_out);
  and and_8 (and_8_out, DataIn[3], not_7_out);
  and and_9 (and_9_out, not_5_out, not_7_out);
  and and_10 (and_10_out, DataIn[4], not_7_out);
  and and_11 (and_11_out, not_6_out, not_7_out);
  and and_12 (and_12_out, Dataout[0], and_1_out);
  and and_13 (and_13_out, Dataout[1], Dataout[0], and_1_out);
  and and_14 (and_14_out, Dataout[2], Dataout[1], Dataout[0], and_1_out);
  and and_15 (and_15_out, Dataout[3], Dataout[2], Dataout[1], Dataout[0], and_1_out);
  and and_16 (Cout, Dataout[4], Dataout[3], Dataout[2], Dataout[1], Dataout[0], and_1_out);
  or or_1 (or_1_out, and_2_out, and_1_out);
  or or_2 (or_2_out, and_1_out, and_3_out);
  or or_3 (or_3_out, and_4_out, and_12_out);
  or or_4 (or_4_out, and_12_out, and_5_out);
  or or_5 (or_5_out, and_6_out, and_13_out);
  or or_6 (or_6_out, and_13_out, and_7_out);
  or or_7 (or_7_out, and_8_out, and_14_out);
  or or_8 (or_8_out, and_14_out, and_9_out);
  or or_9 (or_9_out, and_10_out, and_15_out);
  or or_10 (or_10_out, and_15_out, and_11_out);
  J_K_Flip_Flop j_k_ff_1 (
    .J(or_1_out), .clk(clock), .K(or_2_out), .Q(Dataout[0]), .reset(reset));  // open: Qn, preset, en
  J_K_Flip_Flop j_k_ff_2 (
    .J(or_3_out), .clk(clock), .K(or_4_out), .Q(Dataout[1]), .reset(reset));  // open: Qn, preset, en
  J_K_Flip_Flop j_k_ff_3 (
    .J(or_5_out), .clk(clock), .K(or_6_out), .Q(Dataout[2]), .reset(reset));  // open: Qn, preset, en
  J_K_Flip_Flop j_k_ff_4 (
    .J(or_7_out), .clk(clock), .K(or_8_out), .Q(Dataout[3]), .reset(reset));  // open: Qn, preset, en
  J_K_Flip_Flop j_k_ff_5 (
    .J(or_9_out), .clk(clock), .K(or_10_out), .Q(Dataout[4]), .reset(reset));  // open: Qn, preset, en

  // Notes on the sheet:
  //   2207042
endmodule

// MBR c2
module MBR_counter_2_bit (
  input  Count,
  input  Load,
  input  DATAin1,
  input  DATAin2,
  input  Clock,
  input  Reset,
  output DATAout1,
  output DATAout2,
  output Cout
);

  wire and_1_out, and_2_out, and_3_out, and_4_out, and_5_out, and_6_out, not_1_out, not_2_out, not_3_out,
       not_4_out, or_1_out, or_2_out, or_3_out, or_4_out;

  not not_1 (not_1_out, DATAin1);
  not not_2 (not_2_out, DATAin2);
  and and_1 (and_1_out, Count, not_4_out);
  not not_3 (not_3_out, not_4_out);
  not not_4 (not_4_out, Load);
  and and_2 (and_2_out, DATAin1, not_3_out);
  and and_3 (and_3_out, not_1_out, not_3_out);
  and and_4 (and_4_out, DATAin2, not_3_out);
  and and_5 (and_5_out, not_2_out, not_3_out);
  and and_6 (and_6_out, DATAout1, and_1_out);
  and and_7 (Cout, DATAout2, DATAout1, and_1_out);
  or or_1 (or_1_out, and_2_out, and_1_out);
  or or_2 (or_2_out, and_1_out, and_3_out);
  or or_3 (or_3_out, and_4_out, and_6_out);
  or or_4 (or_4_out, and_6_out, and_5_out);
  J_K_Flip_Flop j_k_ff_1 (
    .J(or_1_out), .clk(Clock), .K(or_2_out), .Q(DATAout1), .reset(Reset));  // open: Qn, preset, en
  J_K_Flip_Flop j_k_ff_2 (
    .J(or_3_out), .clk(Clock), .K(or_4_out), .Q(DATAout2), .reset(Reset));  // open: Qn, preset, en

  // Notes on the sheet:
  //   2207042
endmodule
