// Logisim project alifff.circ as structural Verilog: 6 circuits, main circuit main
module main (
  input  [21:0] A,
  input  [21:0] B,
  input  [1:0] CONTROL,
  output [21:0] OUTPUT
);

  wire [21:0] and_1_a_and_b, n22_bit_a_s_1_out_4, xor_1_a_xor_b;

  \and  and_1 (.A(A), .B(B), .A_and_B(and_1_a_and_b));
  \xor  xor_1 (.A(A), .B(B), .A_xor_B(xor_1_a_xor_b));
  _22_bit_a_s u_22_bit_a_s_1 (.C_IN(CONTROL[0]), .A(A), .B(B), .out_4(n22_bit_a_s_1_out_4));  // open: cout_1, cout
  Multiplexer #(.select(2), .width(22)) multiplexer_1 (
    .in0(and_1_a_and_b), .in1(xor_1_a_xor_b), .in2(n22_bit_a_s_1_out_4), .in3(n22_bit_a_s_1_out_4),
    .out(OUTPUT), .sel(CONTROL));  // open: en
endmodule

module \and  (
  input  [21:0] A,
  input  [21:0] B,
  output [21:0] A_and_B
);

  assign A_and_B = A & B;  // AND_Gate and_1, 22 bits wide
endmodule

module \xor  (
  input  [21:0] A,
  input  [21:0] B,
  output [21:0] A_xor_B
);

  assign A_xor_B = A ^ B;  // XOR_Gate xor_1, 22 bits wide
endmodule

module _4_bit_carry_generator (
  input  C_IN,
  input  G_0,
  input  P_0,
  input  G_1,
  input  P_1,
  input  G_2,
  input  P_2,
  input  G_3,
  input  P_3,
  output C_1,
  output C_2,
  output C_3,
  output C_4
);

  wire and_1_out, and_2_out, and_3_out, and_4_out, and_5_out, and_6_out, and_7_out, and_8_out, and_9_out,
       and_10_out;

  and and_1 (and_1_out, C_IN, P_0);
  and and_2 (and_2_out, G_0, P_1);
  or or_1 (C_1, and_1_out, G_0);
  and and_3 (and_3_out, and_1_out, P_1);
  and and_4 (and_4_out, G_1, P_2);
  and and_5 (and_5_out, P_2, P_1, G_0);
  and and_6 (and_6_out, P_2, P_1, P_0, C_IN);
  or or_2 (C_2, and_3_out, and_2_out, G_1);
  and and_7 (and_7_out, G_2, P_3);
  and and_8 (and_8_out, P_2, P_3, G_1);
  and and_9 (and_9_out, P_3, P_2, P_1, G_0);
  and and_10 (and_10_out, P_3, P_2, P_1, P_0, C_IN);
  or or_3 (C_3, G_2, and_4_out, and_5_out, and_6_out);
  or or_4 (C_4, G_3, and_7_out, and_8_out, and_9_out, and_10_out);
endmodule

module _4_bit_cla (
  input  C_IN,
  input  [3:0] A,
  input  [3:0] B,
  output C_3,
  output C_4,
  output [3:0] S
);

  wire n4_bit_carry_generator_1_c_1, n4_bit_carry_generator_1_c_2;
  wire [3:0] G_out, P_out;

  assign G_out = A & B;  // AND_Gate G, 4 bits wide
  assign P_out = A ^ B;  // XOR_Gate P, 4 bits wide
  _4_bit_carry_generator u_4_bit_carry_generator_1 (
    .C_IN(C_IN), .G_0(G_out[0]), .P_0(P_out[0]), .G_1(G_out[1]), .P_1(P_out[1]), .G_2(G_out[2]),
    .P_2(P_out[2]), .G_3(G_out[3]), .P_3(P_out[3]), .C_1(n4_bit_carry_generator_1_c_1),
    .C_2(n4_bit_carry_generator_1_c_2), .C_3(C_3), .C_4(C_4));
  xor S_0 (S[0], P_out[0], C_IN);
  xor S_1 (S[1], P_out[1], n4_bit_carry_generator_1_c_1);
  xor S_2 (S[2], P_out[2], n4_bit_carry_generator_1_c_2);
  xor S_4 (S[3], P_out[3], C_3);
endmodule

module _22_bit_a_s (
  input  C_IN,
  input  [21:0] A,
  input  [21:0] B,
  output [21:0] out_4,
  output cout_1,
  output cout
);

  wire n4_bit_cla_1_c_4, n4_bit_cla_2_c_4, n4_bit_cla_3_c_4, n4_bit_cla_4_c_4, n4_bit_cla_5_c_4;
  wire [21:0] bit_extender_1_out, xor_1_out;

  assign bit_extender_1_out = {{21{C_IN}}, C_IN};  // Bit_Extender bit_extender_1
  assign xor_1_out = bit_extender_1_out ^ B;  // XOR_Gate xor_1, 22 bits wide
  _4_bit_cla u_4_bit_cla_1 (
    .C_IN(C_IN), .A(A[3:0]), .B(xor_1_out[3:0]), .C_4(n4_bit_cla_1_c_4), .S(out_4[3:0]));  // open: C_3
  _4_bit_cla u_4_bit_cla_2 (
    .C_IN(n4_bit_cla_1_c_4), .A(A[7:4]), .B(xor_1_out[7:4]), .C_4(n4_bit_cla_2_c_4), .S(out_4[7:4]));  // open: C_3
  _4_bit_cla u_4_bit_cla_3 (
    .C_IN(n4_bit_cla_2_c_4), .A(A[15:12]), .B(xor_1_out[11:8]), .C_4(n4_bit_cla_3_c_4), .S(out_4[11:8]));  // open: C_3
  _4_bit_cla u_4_bit_cla_4 (
    .C_IN(n4_bit_cla_3_c_4), .A(A[15:12]), .B(xor_1_out[15:12]), .C_4(n4_bit_cla_4_c_4), .S(out_4[15:12]));  // open: C_3
  _4_bit_cla u_4_bit_cla_5 (
    .C_IN(n4_bit_cla_4_c_4), .A(A[19:16]), .B(xor_1_out[19:16]), .C_4(n4_bit_cla_5_c_4), .S(out_4[19:16]));  // open: C_3
  Adder #(.width(1)) adder_1 (.a(A[20]), .b(xor_1_out[20]), .out(out_4[20]), .cin(n4_bit_cla_5_c_4), .cout(cout_1));
  Adder #(.width(1)) adder_2 (.a(A[21]), .b(xor_1_out[21]), .out(out_4[21]), .cin(cout_1), .cout(cout));

  assign A[11:8] = A[15:12];
endmodule
