// Logisim project computer-2207042.circ as structural Verilog: 3 circuits, main circuit main
module main (
  input  reset
);

  wire clock_1_out, control_unit_1_load, control_unit_1_out_clk, control_unit_1_store;
  wire [4:0] control_unit_1_mar_out;
  wire [21:0] control_unit_1_data_out, ram_1_data;

  Clock clock_1 (.out(clock_1_out));
  control_unit control_unit_1 (
    .reset(reset), .clock(clock_1_out), .data_in(ram_1_data), .Data_out(control_unit_1_data_out),
    .out_clk(control_unit_1_out_clk), .load(control_unit_1_load), .mar_out(control_unit_1_mar_out),
    .store(control_unit_1_store));
  RAM #(.addrWidth(5), .dataWidth(22), .bus("separate")) ram_1 (
    .addr(control_unit_1_mar_out), .din(control_unit_1_data_out), .data(ram_1_data),
    .str(control_unit_1_store), .clk(control_unit_1_out_clk), .ld(control_unit_1_load));  // open: sel, clr

  // Notes on the sheet:
  //   ASHRAFUL HOSEN
  //   ROLL:2207042
endmodule

module control_unit (
  input  reset,
  input  clock,
  input  [21:0] data_in,
  output out_clk,
  output load,
  output [4:0] mar_out,
  output store,
  output [21:0] Data_out
);

  wire ac_mbr, add, alu_add, alu_and, alu_sub, alu_xor, \and , and_18_out, bsb, bun, Bz, dec, f, f0, f1,
       halt, ir_mbr, isz, load_t, M_mbr_1, M_mbr_2, M_mbr_3, mar_b_ad, mar_pc, mbr_1, mbr_ac, mbr_ad__pc,
       mbr_inc, mbr_M_1, mbr_M_2, multiplexer_8_out, not_1_out, not_2_out, not_3_out, not_4_out, not_5_out,
       or_2_out, or_3_out, or_4_out, or_6_out, or_7_out, or_8_out, or_9_out, or_10_out, pc_b_ad, pc_inc_2,
       sto, t0, t1, t2, t3, \xor ;
  wire [1:0] alu_controller_1_out_5, counter_1_q;
  wire [3:0] bit_extender_1_out, ir_out;
  wire [4:0] address, multiplexer_1_out, multiplexer_6_out;
  wire [19:0] new_mbr;
  wire [21:0] ac_in, ac_out, main_1_output, multiplexer_2_out, multiplexer_3_out, multiplexer_4_out;
  wire [21:5] mbr_out;

  Decoder #(.select(4)) decoder_1 (
    .out0(\and ), .out1(add), .out2(sto), .out3(isz), .out4(bsb), .out5(bun), .out6(load_t), .out7(halt),
    .out8(\xor ), .out9(dec), .sel(ir_out));  // open: out10, out11, out12, out13, out14, out15, en
  not not_1 (not_1_out, f);
  and and_1 (mar_pc, not_1_out, t0);
  not not_2 (not_2_out, f);
  and and_2 (mbr_M_1, not_2_out, t1);
  not not_3 (not_3_out, f);
  and and_3 (ir_mbr, not_3_out, t2);
  and and_4 (alu_and, f, \and , t2);
  and and_5 (alu_add, f, add, t2);
  Multiplexer #(.width(5), .enable("false")) multiplexer_1 (
    .in0(new_mbr[4:0]), .in1(address), .out(multiplexer_1_out), .sel(mar_b_ad));
  Counter #(.width(2), .max('h3)) counter_1 (
    .Q(counter_1_q), .clk(out_clk), .clr(reset));  // open: load, D, count, carry
  or or_1 (load, mbr_M_1, mbr_M_2);
  Multiplexer #(.select(2), .width(22)) multiplexer_2 (
    .in0(data_in), .in1({2'b00, new_mbr[19:16], {11{1'b0}}, new_mbr[4:0]}), .in2(ac_out),
    .out(multiplexer_2_out), .sel({mbr_ac, mbr_ad__pc}));  // open: in3, en
  or or_2 (or_2_out, mar_pc, mar_b_ad);
  Multiplexer #(.width(22), .enable("false")) multiplexer_3 (
    .in0(ac_in), .in1({mbr_out, address}), .out(multiplexer_3_out), .sel(ac_mbr));
  Decoder #(.select(2)) decoder_2 (.out0(t0), .out1(t1), .out2(t2), .out3(t3), .sel(counter_1_q));  // open: en
  or or_3 (or_3_out, load, mbr_ac, mbr_ad__pc, mbr_1);
  Multiplexer #(.width(22)) multiplexer_4 (
    .in0(multiplexer_2_out), .in1(22'h1), .out(multiplexer_4_out), .sel(mbr_1));  // open: en
  or or_4 (or_4_out, alu_add, alu_xor, alu_and, alu_sub, ac_mbr);
  J_K_Flip_Flop j_k_ff_1 (.J(f1), .clk(out_clk), .K(f0), .Q(f));  // open: Qn, preset, en, reset
  MBR u_mbr_1 (
    .Count(mbr_inc), .Load(or_3_out), .DataIn(multiplexer_4_out), .clock(out_clk), .reset(reset),
    .Dataout({mbr_out, address}));
  MAR mar_1 (.Load(or_2_out), .DataIn(multiplexer_1_out), .clock(out_clk), .reset(reset), .Dataout(mar_out));
  AC ac_1 (.Load(or_4_out), .DataIn(multiplexer_3_out), .clock(out_clk), .reset(reset), .Dataout(ac_out));
  and and_6 (M_mbr_2, f, isz, t3);
  and and_7 (mbr_inc, f, isz, t2);
  and and_8 (ac_mbr, f, load_t, t2);
  or or_5 (store, M_mbr_1, M_mbr_2, M_mbr_3);
  not not_4 (not_4_out, halt);
  and and_9 (pc_b_ad, bun, t3);
  and and_10 (mar_b_ad, f, t0);
  and and_11 (M_mbr_1, f, sto, t3);
  and and_12 (alu_xor, f, \xor , t2);
  nor nor_1 (Bz, address[0], address[1], address[2], address[3], address[4], mbr_out[5], mbr_out[6], mbr_out[7], mbr_out[8], mbr_out[9], mbr_out[10], mbr_out[12], mbr_out[13], mbr_out[14], mbr_out[15], mbr_out[16], mbr_out[17], mbr_out[18], mbr_out[19], mbr_out[20], mbr_out[21], mbr_out[11]);
  Multiplexer #(.width(22), .enable("false")) multiplexer_5 (
    .in0(data_in), .in1({mbr_out, address}), .out(Data_out), .sel(store));
  and and_13 (out_clk, clock, not_4_out);
  IR ir_1 (.Load(ir_mbr), .DataIn(mbr_out[19:16]), .clock(out_clk), .reset(reset), .Dataout(ir_out));
  and and_14 (mbr_ac, f, sto, t2);
  and and_15 (alu_sub, f, dec, t3);
  and and_16 (mbr_1, f, dec, t2);
  ALU_controller alu_controller_1 (
    .\and (alu_and), .\xor (alu_xor), .add(alu_add), .sub(alu_sub), .out_5(alu_controller_1_out_5));
  assign bit_extender_1_out = {{3{mbr_ad__pc}}, mbr_ad__pc};  // Bit_Extender bit_extender_1
  Multiplexer #(.width(5), .enable("false")) multiplexer_6 (
    .in0(mar_out), .in1(address), .out(multiplexer_6_out), .sel(pc_b_ad));
  or or_6 (or_6_out, mbr_M_1, pc_inc_2, M_mbr_3);
  assign new_mbr[19:16] = bit_extender_1_out & 4'b0101;  // AND_Gate and_17, 4 bits wide
  or or_7 (or_7_out, alu_and, alu_xor, alu_add, alu_sub);
  and and_18 (and_18_out, or_7_out, multiplexer_8_out);
  alifff_main main_1 (.A(ac_out), .B({mbr_out, address}), .CONTROL(alu_controller_1_out_5), .OUTPUT(main_1_output));
  and and_19 (pc_inc_2, Bz, f, isz, t3);
  and and_20 (mbr_ad__pc, f, bsb, t2);
  and and_21 (M_mbr_3, f, bsb, t3);
  or or_8 (or_8_out, mbr_ad__pc, pc_b_ad);
  Multiplexer #(.width(22), .enable("false")) multiplexer_7 (
    .in0(ac_out), .in1(main_1_output), .out(ac_in), .sel(and_18_out));
  or or_9 (or_9_out, dec, \xor , add, \and , sto, isz, bsb, load_t, halt);
  or or_10 (or_10_out, add, \and , isz, load_t, \xor , dec);
  Multiplexer multiplexer_8 (.in0(t2), .in1(t3), .out(multiplexer_8_out), .sel(alu_sub));  // open: en
  not not_5 (not_5_out, f);
  and and_22 (f0, f, t3);
  and and_23 (mbr_M_2, f, or_10_out, t1);
  PC pc_1 (
    .Count(or_6_out), .Load(or_8_out), .DataIn(multiplexer_6_out), .clock(out_clk), .reset(reset),
    .Dataout(new_mbr[4:0]));
  and and_24 (f1, not_5_out, or_9_out, t3);

  // Other names for the same wires on the sheet: mbr_op__0101 = mbr_ad__pc; pc_mar = mbr_ad__pc; clk = out_clk;
  //   mbr_out[4:0] = address; opcode[3:0] = mbr_out[19:16]; pc_out[4:0] = new_mbr[4:0]; pc_inc_1 = mbr_M_1;
  //   pc_inc_3 = M_mbr_3; rst = reset
endmodule

module ALU_controller (
  input  \and ,
  input  \xor ,
  input  add,
  input  sub,
  output [1:0] out_5
);

  Priority_Encoder #(.select(2)) priority_encoder_1 (
    .in0(\and ), .in1(\xor ), .in2(add), .in3(sub), .out(out_5));  // open: gs, en_out, en_in
endmodule
